// Logisim project Lucas_de_Souza_Cerveira_Pereira.circ as structural Verilog: 7 circuits, main circuit main
module somador_1bit (
  input  c_in,
  input  a,
  input  b,
  output out_4,
  output out_5
);

  wire and_1_out, and_2_out, and_3_out, xor_1_out;

  xor xor_1 (xor_1_out, a, b);
  xor xor_2 (out_4, xor_1_out, c_in);
  and and_1 (and_1_out, a, c_in);
  and and_2 (and_2_out, a, b);
  and and_3 (and_3_out, b, c_in);
  or or_1 (out_5, and_1_out, and_2_out, and_3_out);
endmodule

module main (
  input  [7:0] in_1,
  input  in_2,
  input  in_3,
  input  in_4,
  input  in_5,
  input  in_6,
  input  in_7,
  input  in_8,
  input  in_9,
  output [7:0] out_10
);

  wire [7:0] registradorsetenable_1_out_4, registradorsetenable_2_out_4, registradorsetenable_3_out_4;

  registradorsetenable registradorsetenable_1 (
    .in_1(in_1), .in_2(in_2), .in_3(in_3), .out_4(registradorsetenable_1_out_4));
  registradorsetenable registradorsetenable_2 (
    .in_1(registradorsetenable_1_out_4), .in_2(in_4), .in_3(in_5), .out_4(registradorsetenable_2_out_4));
  registradorsetenable registradorsetenable_3 (
    .in_1(registradorsetenable_2_out_4), .in_2(in_6), .in_3(in_7), .out_4(registradorsetenable_3_out_4));
  registradorsetenable registradorsetenable_4 (
    .in_1(registradorsetenable_3_out_4), .in_2(in_8), .in_3(in_9), .out_4(out_10));

  // Notes on the sheet:
  //   Lucas de Souza Cerveira Pereira
endmodule

module somador_8bit (
  input  in_1,
  input  [7:0] in_2,
  input  [7:0] in_3,
  output [7:0] out_4,
  output out_5
);

  wire somador_1bit_1_out_5, somador_1bit_2_out_5, somador_1bit_3_out_5, somador_1bit_4_out_5,
       somador_1bit_5_out_5, somador_1bit_6_out_5, somador_1bit_7_out_5;

  somador_1bit somador_1bit_1 (.a(in_2[0]), .b(in_3[0]), .c_in(in_1), .out_4(out_4[0]), .out_5(somador_1bit_1_out_5));
  somador_1bit somador_1bit_2 (
    .a(in_2[1]), .b(in_3[1]), .c_in(somador_1bit_1_out_5), .out_4(out_4[1]), .out_5(somador_1bit_2_out_5));
  somador_1bit somador_1bit_3 (
    .a(in_2[2]), .b(in_3[2]), .c_in(somador_1bit_2_out_5), .out_4(out_4[2]), .out_5(somador_1bit_3_out_5));
  somador_1bit somador_1bit_4 (
    .a(in_2[3]), .b(in_3[3]), .c_in(somador_1bit_3_out_5), .out_4(out_4[3]), .out_5(somador_1bit_4_out_5));
  somador_1bit somador_1bit_5 (
    .a(in_2[4]), .b(in_3[4]), .c_in(somador_1bit_4_out_5), .out_4(out_4[4]), .out_5(somador_1bit_5_out_5));
  somador_1bit somador_1bit_6 (
    .a(in_2[5]), .b(in_3[5]), .c_in(somador_1bit_5_out_5), .out_4(out_4[5]), .out_5(somador_1bit_6_out_5));
  somador_1bit somador_1bit_7 (
    .a(in_2[6]), .b(in_3[6]), .c_in(somador_1bit_6_out_5), .out_4(out_4[6]), .out_5(somador_1bit_7_out_5));
  somador_1bit somador_1bit_8 (.a(in_2[7]), .b(in_3[7]), .c_in(somador_1bit_7_out_5), .out_4(out_4[7]), .out_5(out_5));
endmodule

module memory_1bit (
  input  in_1,
  input  in_2,
  output out_3
);

  wire nand_1_out, nand_2_out, nand_4_out;

  nand nand_1 (nand_1_out, in_1, in_2);
  nand nand_2 (nand_2_out, in_2, nand_1_out);
  nand nand_3 (out_3, nand_1_out, nand_4_out);
  nand nand_4 (nand_4_out, out_3, nand_2_out);
endmodule

module registrador (
  input  [7:0] in_1,
  input  in_2,
  output [7:0] out_3
);

  memory_1bit memory_1bit_1 (.in_1(in_1[0]), .in_2(in_2), .out_3(out_3[0]));
  memory_1bit memory_1bit_2 (.in_1(in_1[1]), .in_2(in_2), .out_3(out_3[1]));
  memory_1bit memory_1bit_3 (.in_1(in_1[2]), .in_2(in_2), .out_3(out_3[2]));
  memory_1bit memory_1bit_4 (.in_1(in_1[3]), .in_2(in_2), .out_3(out_3[3]));
  memory_1bit memory_1bit_5 (.in_1(in_1[4]), .in_2(in_2), .out_3(out_3[4]));
  memory_1bit memory_1bit_6 (.in_1(in_1[5]), .in_2(in_2), .out_3(out_3[5]));
  memory_1bit memory_1bit_7 (.in_1(in_1[6]), .in_2(in_2), .out_3(out_3[6]));
  memory_1bit memory_1bit_8 (.in_1(in_1[7]), .in_2(in_2), .out_3(out_3[7]));
endmodule

module enable (
  input  [7:0] in_1,
  input  in_2,
  output [7:0] out_3
);

  and and_1 (out_3[0], in_1[0], in_2);
  and and_2 (out_3[1], in_1[1], in_2);
  and and_3 (out_3[2], in_1[2], in_2);
  and and_4 (out_3[3], in_1[3], in_2);
  and and_5 (out_3[4], in_1[4], in_2);
  and and_6 (out_3[5], in_1[5], in_2);
  and and_7 (out_3[6], in_1[6], in_2);
  and and_8 (out_3[7], in_1[7], in_2);
endmodule

module registradorsetenable (
  input  [7:0] in_1,
  input  in_2,
  input  in_3,
  output [7:0] out_4
);

  wire [7:0] registrador_1_out_3;

  registrador registrador_1 (.in_1(in_1), .in_2(in_2), .out_3(registrador_1_out_3));
  enable enable_1 (.in_1(registrador_1_out_3), .in_2(in_3), .out_3(out_4));
endmodule
